// Logisim project Lab4.circ as structural Verilog: 5 circuits, main circuit main
module main (
);

  wire alu_control_1_p13, and_1_out, clock_1_out, comparator_1_eq, main_control_1_branch,
       main_control_1_memread, main_control_1_memtoreg, main_control_1_memwrite, register_file_1_p5;
  wire [3:0] alu_control_1_p12;
  wire [31:0] adder_1_out, adder_2_out, alu_32_1_p2, data_memory_1_out_6, immgen_1_imm32,
       instruction_memory_1_instruction, multiplexer_2_out, register_1_q, register_file_1_p3,
       register_file_1_p6, register_file_1_p7, register_file_1_p8;

  Clock clock_1 (.out(clock_1_out));
  Register #(.width(32)) register_1 (
    .D(multiplexer_2_out), .en(1'b1), .clk(clock_1_out), .Q(register_1_q));  // open: clr
  Adder #(.width(32)) adder_1 (.a(register_1_q), .b(32'h4), .out(adder_1_out));  // open: cin, cout
  Instruction_Memory instruction_memory_1 (
    .Address(register_1_q[23:0]), .Clock_In(clock_1_out), .Instruction(instruction_memory_1_instruction));
  // ALU_control alu_control_1: pin names not known; wires that end beside it: instruction_memory_1_instruction[30], instruction_memory_1_instruction[14], instruction_memory_1_instruction[13], instruction_memory_1_instruction[12], instruction_memory_1_instruction[6], instruction_memory_1_instruction[5], instruction_memory_1_instruction[4], instruction_memory_1_instruction[11:7], alu_control_1_p12[3], alu_control_1_p12[2], alu_control_1_p12[1], alu_control_1_p12[0], alu_control_1_p13
  ImmGen immgen_1 (.Instruction(instruction_memory_1_instruction), .IMM32(immgen_1_imm32));
  // Register_file register_file_1: pin names not known; wires that end beside it: instruction_memory_1_instruction[19:15], instruction_memory_1_instruction[24:20], register_file_1_p3, clock_1_out, register_file_1_p5, register_file_1_p6, register_file_1_p7, register_file_1_p8, register_file_1_p6
  Main_Control main_control_1 (
    .i6_0(instruction_memory_1_instruction[6:0]), .MemtoReg(main_control_1_memtoreg),
    .RegWrite(register_file_1_p5), .MemRead(main_control_1_memread), .MemWrite(main_control_1_memwrite),
    .Branch(main_control_1_branch));
  Multiplexer #(.enable("false"), .width(32)) multiplexer_1 (
    .in0(register_file_1_p7), .in1(immgen_1_imm32), .out(register_file_1_p8), .sel(alu_control_1_p13));
  Comparator #(.width(32)) comparator_1 (
    .a(register_file_1_p6), .b(register_file_1_p7), .eq(comparator_1_eq));  // open: gt, lt
  // ALU_32 alu_32_1: pin names not known; wires that end beside it: alu_control_1_p12, alu_32_1_p2
  Adder #(.width(32)) adder_2 (.a(register_1_q), .b(immgen_1_imm32), .out(adder_2_out));  // open: cin, cout
  and and_1 (and_1_out, main_control_1_branch, comparator_1_eq);
  Multiplexer #(.enable("false"), .width(32)) multiplexer_2 (
    .in0(adder_1_out), .in1(adder_2_out), .out(multiplexer_2_out), .sel(and_1_out));
  Data_Memory data_memory_1 (
    .Address(alu_32_1_p2[25:0]), .Mem_Write(main_control_1_memwrite), .Mem_Read(main_control_1_memread),
    .Clock_In(clock_1_out), .Write_Data(register_file_1_p7), .out_6(data_memory_1_out_6));
  Multiplexer #(.enable("false"), .width(32)) multiplexer_3 (
    .in0(alu_32_1_p2), .in1(data_memory_1_out_6), .out(register_file_1_p3), .sel(main_control_1_memtoreg));
endmodule

module ImmGen (
  input  [31:0] Instruction,
  output [31:0] IMM32
);

  Multiplexer #(.enable("false"), .width(4)) multiplexer_1 (
    .in0(Instruction[24:21]), .in1(Instruction[11:8]), .out(IMM32[4:1]), .sel(Instruction[5]));
  Multiplexer #(.enable("false")) multiplexer_2 (
    .in0(Instruction[31]), .in1(Instruction[7]), .out(IMM32[11]), .sel(Instruction[6]));
  Multiplexer #(.enable("false"), .select(2)) multiplexer_3 (
    .in0(Instruction[20]), .in1(Instruction[7]), .in3(1'b0), .out(IMM32[0]), .sel(Instruction[6:5]));  // open: in2
  assign IMM32[31:12] = {{19{Instruction[31]}}, Instruction[31]};  // Bit_Extender bit_extender_1

  assign IMM32[10:5] = Instruction[30:25];

  // Other names for the same wires on the sheet: i30_25[5:0] = Instruction[30:25]; i5 = Instruction[5];
  //   i6_5[1:0] = Instruction[6:5]; i6 = Instruction[6]; i7 = Instruction[7]; i11_8[3:0] = Instruction[11:8];
  //   i20 = Instruction[20]; i24_21[3:0] = Instruction[24:21]; i31 = Instruction[31]
endmodule

module Main_Control (
  input  [6:0] i6_0,
  output MemtoReg,
  output RegWrite,
  output MemRead,
  output MemWrite,
  output Branch
);

  wire not_1_out, not_2_out;

  not not_1 (not_1_out, i6_0[6]);
  not not_2 (not_2_out, i6_0[5]);
  not not_3 (MemtoReg, i6_0[4]);
  or or_1 (RegWrite, not_2_out, i6_0[4]);
  and and_1 (MemRead, not_2_out, MemtoReg);
  and and_2 (MemWrite, not_1_out, i6_0[5], MemtoReg);

  assign Branch = i6_0[6];
endmodule

module Instruction_Memory (
  input  [23:0] Address,
  input  Clock_In,
  output [31:0] Instruction
);

  wire not_1_out;

  not not_1 (not_1_out, Clock_In);
  RAM #(.addrWidth(22), .asyncread("true"), .dataWidth(32)) ram_1 (
    .addr(Address[23:2]), .we(1'b0), .oe(not_1_out), .dout(Instruction));  // open: clk, din
endmodule

module Data_Memory (
  input  [25:0] Address,
  input  Mem_Write,
  input  Mem_Read,
  input  Clock_In,
  input  [31:0] Write_Data,
  output [31:0] out_6
);

  RAM #(.addrWidth(24), .asyncread("true"), .dataWidth(32)) ram_1 (
    .addr(Address[25:2]), .we(Mem_Write), .oe(Mem_Read), .clk(Clock_In), .din(Write_Data), .dout(out_6));
endmodule
